// Logisim project project 1.circ as structural Verilog: 2 circuits, main circuit solution
module solution (
  input  [5:0] A,
  input  [5:0] B,
  output [5:0] R,
  output C_out,
  output V
);

  wire not_1_out, not_2_out, not_3_out, not_4_out, not_5_out, not_6_out, one_bit_adder_1_c_out,
       one_bit_adder_2_c_out, one_bit_adder_3_c_out, one_bit_adder_4_c_out, one_bit_adder_6_c_out;

  // Probe on A
  // Probe on B
  not not_1 (not_1_out, B[0]);
  not not_2 (not_2_out, B[1]);
  not not_3 (not_3_out, B[2]);
  not not_4 (not_4_out, B[3]);
  not not_5 (not_5_out, B[4]);
  not not_6 (not_6_out, B[5]);
  one_bit_adder one_bit_adder_1 (.A(A[0]), .B(not_1_out), .C_in(1'b1), .SUM(R[0]), .C_out(one_bit_adder_1_c_out));
  one_bit_adder one_bit_adder_2 (
    .A(A[2]), .B(not_3_out), .C_in(one_bit_adder_6_c_out), .SUM(R[2]), .C_out(one_bit_adder_2_c_out));
  one_bit_adder one_bit_adder_3 (
    .A(A[3]), .B(not_4_out), .C_in(one_bit_adder_2_c_out), .SUM(R[3]), .C_out(one_bit_adder_3_c_out));
  one_bit_adder one_bit_adder_4 (
    .A(A[4]), .B(not_5_out), .C_in(one_bit_adder_3_c_out), .SUM(R[4]), .C_out(one_bit_adder_4_c_out));
  one_bit_adder one_bit_adder_5 (.A(A[5]), .B(not_6_out), .C_in(one_bit_adder_4_c_out), .SUM(R[5]), .C_out(C_out));
  one_bit_adder one_bit_adder_6 (
    .A(A[1]), .B(not_2_out), .C_in(one_bit_adder_1_c_out), .SUM(R[1]), .C_out(one_bit_adder_6_c_out));
  xor xor_1 (V, one_bit_adder_4_c_out, C_out);
  // Probe on R
endmodule

module one_bit_adder (
  input  A,
  input  B,
  input  C_in,
  output SUM,
  output C_out
);

  wire and_1_out, and_2_out, and_3_out;

  and and_1 (and_1_out, A, B);
  and and_2 (and_2_out, C_in, B);
  and and_3 (and_3_out, A, C_in);
  xor xor_1 (SUM, A, B, C_in);
  or or_1 (C_out, and_1_out, and_2_out, and_3_out);
endmodule
